// Digital circuit RISCV_Top.dig as structural Verilog
module RISCV_Top (
  input  clk,
  input  rst,
  output [31:0] out_3,
  output [7:0] out_4,
  output [2:0] funct3,
  output [31:0] instr,
  output [6:0] funct7,
  output [6:0] opcode,
  output [4:0] rd,
  output [4:0] rs1,
  output [4:0] rs2,
  output [1:0] ALUOp,
  output [3:0] ALUControl,
  output [31:0] WriteData,
  output [31:0] RD1,
  output [31:0] RD2,
  output [31:0] imm
);

  wire ALUSrc, and_3_out, and_4_out, and_5_out, and_6_out, Branch, clk_t, comparator_1_eq, decoder_1_out_0,
       decoder_1_out_1, decoder_1_out_4, decoder_1_out_5, Jal, Jalr, MemRead, MemtoReg, MemWrite, not_1_out,
       not_2_out, not_3_out, or_2_out, P1, P2, P3, P4, P5, P6, RegWrite, regWrite_t, takeBranch, write_jal,
       Zero;
  wire [15:0] D1, D2, D3, D4, D5, D6;
  wire [31:0] ALU_in2, Jalr_Adder_s, multiplexer_1_out, multiplexer_2_out, PC_branch, PC_jalr_target,
       PC_next, PC_plus4, ReadData, Result, WriteData_from_mem;

  Multiplexer #(.Bits(32)) multiplexer_1 (.sel(takeBranch), .in_0(PC_plus4), .in_1(PC_branch), .out(multiplexer_1_out));
  D_FF_AS #(.Bits(32)) Program_Counter (.Set(1'b0), .D(PC_next), .C(clk_t), .Clr(rst), .Q(out_3));  // open: nQ
  Comparator #(.Bits(5)) comparator_1 (.a(instr[11:7]), .b({5{1'b0}}), .eq(comparator_1_eq));  // open: gt, lt
  Multiplexer #(.Bits(32)) multiplexer_2 (
    .sel(Jal), .in_0(multiplexer_1_out), .in_1(PC_branch), .out(multiplexer_2_out));
  or or_1 (write_jal, Jal, Jalr);
  not not_1 (not_1_out, comparator_1_eq);
  Button Hand_Clock (.out(clk_t));
  and and_1 (regWrite_t, RegWrite, not_1_out);
  Multiplexer #(.Bits(32)) multiplexer_3 (.sel(Jalr), .in_0(multiplexer_2_out), .in_1(PC_jalr_target), .out(PC_next));
  SixteenSeg sixteenseg_1 (.led(D1), .dp(P1));
  Add #(.Bits(32)) PC_Adder (.a(out_3), .b(32'h4), .c_i(1'b0), .s(PC_plus4));  // open: c_o
  Add #(.Bits(32)) Branch_Adder (.a(out_3), .b(imm), .c_i(1'b0), .s(PC_branch));  // open: c_o
  ROM #(.AddrBits(8), .Bits(32)) Instruction_Memory (
    .A(out_3[9:2]), .sel(1'b1), .D({funct7, instr[24:15], funct3, instr[11:0]}));
  SixteenSeg sixteenseg_2 (.led(D2), .dp(P2));
  SixteenSeg sixteenseg_3 (.led(D3), .dp(P3));
  Add #(.Bits(32)) Jalr_Adder (.a(RD2), .b(imm), .c_i(1'b0), .s(Jalr_Adder_s));  // open: c_o
  SixteenSeg sixteenseg_4 (.led(D4), .dp(P4));
  SixteenSeg sixteenseg_5 (.led(D5), .dp(P5));
  signExtend Sign_Extend (.instr({funct7, instr[24:15], funct3, instr[11:0]}), .opcode(instr[6:0]), .imm(imm));
  SixteenSeg sixteenseg_6 (.led(D6), .dp(P6));
  assign PC_jalr_target = Jalr_Adder_s & 32'hfffffffe;  // And and_2, 32 bits wide
  controlUnit Control_Unit (
    .opcode(instr[6:0]), .Branch(Branch), .MemRead(MemRead), .MemtoReg(MemtoReg), .ALUOp(ALUOp),
    .MemWrite(MemWrite), .ALUSrc(ALUSrc), .RegWrite(RegWrite), .Jal(Jal), .Jalr(Jalr));  // open: LUI, AUIPC, I, R
  RegisterFile #(.AddrBits(5), .Bits(32)) Register_File (
    .Din(WriteData), .we(regWrite_t), .Rw(instr[11:7]), .C(clk_t), .Ra(instr[19:15]), .Rb(instr[24:20]),
    .Da(RD2), .Db(RD1));
  Decoder #(.Selector_Bits(3)) decoder_1 (
    .sel(funct3), .out_0(decoder_1_out_0), .out_1(decoder_1_out_1), .out_4(decoder_1_out_4),
    .out_5(decoder_1_out_5));  // open: out_2, out_3, out_6, out_7
  Multiplexer #(.Bits(32)) multiplexer_4 (.sel(ALUSrc), .in_0(RD1), .in_1(imm), .out(ALU_in2));
  not not_2 (not_2_out, Zero);
  not not_3 (not_3_out, Result[0]);
  and and_3 (and_3_out, decoder_1_out_0, Zero);
  and and_4 (and_4_out, decoder_1_out_1, not_2_out);
  and and_5 (and_5_out, decoder_1_out_4, Result[0]);
  and and_6 (and_6_out, decoder_1_out_5, not_3_out);
  aluControl ALU_Control (.funct3(funct3), .funct7(funct7), .ALUOp(ALUOp), .ALUControl(ALUControl));
  alu ALU (.A(RD2), .B(ALU_in2), .ALUControl(ALUControl), .Zero(Zero), .Result(Result));
  or or_2 (or_2_out, and_3_out, and_4_out, and_5_out, and_6_out);
  and and_7 (takeBranch, Branch, or_2_out);
  RAMDualPort #(.AddrBits(8), .Bits(32)) Data_Memory (
    .A(Result[9:2]), .Din(RD1), .str(MemWrite), .C(clk_t), .ld(MemRead), .D(ReadData));
  Multiplexer #(.Bits(32)) multiplexer_5 (.sel(MemtoReg), .in_0(Result), .in_1(ReadData), .out(WriteData_from_mem));
  testDisplay testdisplay_1 (
    .D1(D1), .P1(P1), .D2(D2), .P2(P2), .D3(D3), .P3(P3), .D4(D4), .P4(P4), .D5(D5), .P5(P5), .D6(D6),
    .P6(P6), .ALUControl(ALUControl), .opcode(instr[6:0]), .funct3(funct3));
  Multiplexer #(.Bits(32)) multiplexer_6 (.sel(write_jal), .in_0(WriteData_from_mem), .in_1(PC_plus4), .out(WriteData));

  assign {instr[31:25], instr[14:12]} = {funct7, funct3};
  assign opcode = instr[6:0];
  assign out_4 = out_3[9:2];
  assign rd = instr[11:7];
  assign rs1 = instr[24:20];
  assign rs2 = instr[19:15];

  // Other names for the same wires on the sheet: rs1_t[4:0] = instr[19:15]; rs2_t[4:0] = instr[24:20];
  //   PC_jal_target[31:0] = PC_branch; RD1_t[31:0] = RD2; RD2_t[31:0] = RD1; slt_result = Result[0];
  //   WriteData_from_jal[31:0] = PC_plus4

  // Notes on the sheet:
  //   clk: Hz: 5
  //   DEBUGGING SECTION
  //   contents of Instruction_Memory (hex, n*v repeats v):
  //   500513,200593,800613,100693,400713,700793,600393,293,313,813,2030463
  //   ,100413,2830e63,200413,4830863,300413,6830263,400413,6830c63,a000263
  //   ,a5a433,8040463,a004b3,b00533,9005b3,100813,6000a63,b62433,6040663
  //   ,b004b3,c005b3,900633,100813,4000c63,c6a433,4040863,c004b3,d00633
  //   ,9006b3,100813,2000e63,d72433,2040a63,d004b3,e006b3,900733,100813
  //   ,2000063,e7a433,40c63,e004b3,f00733,9007b3,100813,263,130313,fff38413
  //   ,40540433,8324b3,f2049ee3,80863,128293,72a433,f20412e3,63
  //   INSTRUCTION DISPLAY
  //   opcode
  //   funct3
  //   funct7
  //   rs1
  //   rs2
  //   rd
  //   Test Program
  //   addi x1, x0, 10
  //   addi x3, x0, 3
  //   sub x2, x1, x3
  //   ori x4, x2, 0x0F
  //   andi x5, x2, 0x06
  //   slt x6, x5, x4
  //   addi x10, x0, 0x100 
  //   sw x4, 0(x10)        
  //   lw x7, 0(x10)
  //   beq x5, x7, +8      
  //   bne x5, x2, +8       
  //   addi x8, x0, 0xFF    
  //   addi x9, x0, 4
  //   jalr x0, x10, 4
endmodule
